# Fritzing sketch Timo_Sketch (saved by Fritzing 0.9.3b)
breadboards: 1

parts:
  U1 = lolin
  S1 = H-Bridge with L298N
  M1 = DC Motor
  M2 = DC Motor
  VCC1 = Battery
  J1 = Basic Servo
  HC-SR04_Sensor_1 = HC-SR04 Ultrasonic Distance Sensor
  R2 = Resistor [tolerance=±5% resistance=1k package=THT]
  R3 = Resistor [tolerance=±5% resistance=1k package=THT]
  R1 = Resistor [tolerance=±5% resistance=1k package=THT]

nets:
  N1: U1.connector5, HC-SR04_Sensor_1.TRIG
  VCC: U1.connector14, S1.5V, J1.vcc, HC-SR04_Sensor_1.VCC
  N2: U1.connector23, S1.IN4
  N3: U1.connector24, S1.IN3
  N4: U1.connector26, S1.IN2
  N5: U1.connector27, S1.IN1
  N6: U1.connector28, S1.ENA
  N7: U1.connector29, S1.ENB
  N8: U1.connector32, J1.pulse
  GND: U1.connector37, S1.GND, VCC1.-, J1.gnd, HC-SR04_Sensor_1.GND, R3.Pin_0
  N9: S1.12V, VCC1.+
  N10: S1.M1-01, M2.pin_2
  N11: S1.M1-02, M2.pin_1
  N12: S1.M2-01, M1.pin_2
  N13: S1.M2-02, M1.pin_1
  N14: HC-SR04_Sensor_1.ECHO, R1.Pin_0
  N15: R2.Pin_0, R3.Pin_1
  N16: R2.Pin_1, R1.Pin_1

notes:
  7V Spannung

custom parts:
  H-Bridge with L298N: h-bridge
